// Digital circuit Lab3-02.dig as structural Verilog
module Lab3_02 (
  input  [2:0] In,
  input  clk,
  output [7:0] Z
);

  wire and_1_out, and_2_out, and_3_out, and_4_out, and_5_out, and_6_out, and_7_out, and_8_out, not_1_out,
       not_2_out, not_3_out;

  not not_1 (not_1_out, In[2]);
  not not_2 (not_2_out, In[1]);
  not not_3 (not_3_out, In[0]);
  and and_1 (and_1_out, not_1_out, In[1], not_3_out);
  and and_2 (and_2_out, In[2], not_2_out, not_3_out);
  and and_3 (and_3_out, not_1_out, In[1], In[0]);
  and and_4 (and_4_out, In[2], In[1], In[0]);
  and and_5 (and_5_out, not_3_out, not_2_out);
  and and_6 (and_6_out, not_1_out, not_2_out, In[0]);
  and and_7 (and_7_out, In[2], not_2_out);
  and and_8 (and_8_out, In[1], not_3_out);
  or or_1 (Z[6], and_3_out, and_4_out, and_5_out, and_6_out, and_7_out, and_8_out);
  or or_2 (Z[5], and_2_out, and_4_out, and_6_out, and_8_out);
  or or_3 (Z[3], and_3_out, and_6_out, and_7_out);
  or or_4 (Z[2], and_1_out, and_3_out, and_5_out, and_7_out);
  or or_5 (Z[1], and_1_out, and_2_out, and_4_out);
  or or_6 (Z[0], and_2_out, and_6_out, and_8_out);
  Terminal terminal_1 (.D({1'b0, Z[6:5], 1'b0, Z[3:0]}), .C(clk), .en(1'b1));

  assign {Z[7], Z[4]} = 2'b00;
endmodule
