// Digital circuit A-part-circuit.dig as structural Verilog
module A_part_circuit (
  input  I1,
  input  I2,
  input  I3,
  input  I4,
  input  I5,
  input  I6,
  input  I7,
  output C1,
  output C2,
  output C3
);

  xor xor_1 (C1, I4, I5, I6, I7);
  xor xor_2 (C2, I2, I3, I6, I7);
  xor xor_3 (C3, I1, I3, I5, I7);
endmodule
