// Digital circuit Bin-to-2421.dig as structural Verilog
module Bin_to_2421 (
  input  In0,
  input  In1,
  input  In2,
  input  In3,
  input  Selected,
  output Out3,
  output Out2,
  output Out1,
  output Out0
);

  wire C0, C1, C2, C4, In0_t, In1_t, In2_t, or_1_out, or_2_out, or_3_out;

  not not_1 (In0_t, In0);
  not not_2 (In1_t, In1);
  not not_3 (In2_t, In2);
  and and_1 (C0, In1, In2_t);
  and and_2 (C1, In0, In1_t, In2);
  and and_3 (C2, In0_t, In2);
  and and_4 (C4, In2, In1);
  or or_1 (or_1_out, C1, C4, In3);
  or or_2 (or_2_out, C2, C4, In3);
  or or_3 (or_3_out, C0, C1, In3);
  and and_5 (Out3, or_1_out, Selected);
  and and_6 (Out2, or_2_out, Selected);
  and and_7 (Out1, or_3_out, Selected);
  and and_8 (Out0, In0, Selected);

  // Other names for the same wires on the sheet: C3 = In0; C5 = In3; S = Selected
endmodule
