// Digital circuit Bin-to-642-3.dig as structural Verilog
module Bin_to_642_3 (
  input  In0,
  input  In1,
  input  In2,
  input  In3,
  input  Selected,
  output Out3,
  output Out2,
  output Out1,
  output Out0
);

  wire C0, C1, C2, C3, C4, C5, In0_t, In1_t, In2_t, or_1_out, or_2_out, or_3_out, or_4_out;

  not not_1 (In0_t, In0);
  not not_2 (In1_t, In1);
  not not_3 (In2_t, In2);
  and and_1 (C0, In1, In2);
  and and_2 (C1, In0, In1_t, In2_t);
  and and_3 (C2, In0_t, In2);
  and and_4 (C3, In0_t, In1);
  and and_5 (C4, In0, In1_t, In2);
  and and_6 (C5, In0, In1);
  or or_1 (or_1_out, In3, C4, C5);
  or or_2 (or_2_out, C0, C1, C2);
  or or_3 (or_3_out, C3, C4, In3);
  or or_4 (or_4_out, C1, C4, C5);
  and and_7 (Out3, or_1_out, Selected);
  and and_8 (Out2, or_2_out, Selected);
  and and_9 (Out1, or_3_out, Selected);
  and and_10 (Out0, or_4_out, Selected);

  // Other names for the same wires on the sheet: C6 = In3; S = Selected
endmodule
