// Digital circuit Bin-to-Execess-3.dig as structural Verilog
module Bin_to_Execess_3 (
  input  In0,
  input  In1,
  input  In2,
  input  In3,
  input  Selected,
  output Out3,
  output Out2,
  output Out1,
  output Out0
);

  wire C0, C1, C2, C3, C4, C5, C6, In0_t, In1_t, In2_t, or_1_out, or_2_out, or_3_out, or_4_out;

  not not_1 (In0_t, In0);
  not not_2 (In1_t, In1);
  not not_3 (In2_t, In2);
  and and_1 (C0, In0_t, In1_t, In2);
  and and_2 (C1, In0_t, In1, In2_t);
  and and_3 (C2, In0, In2_t);
  and and_4 (C3, In0, In1);
  and and_5 (C4, In0_t, In1, In2);
  and and_6 (C5, In0, In2);
  and and_7 (C6, In0_t, In1_t);
  or or_1 (or_1_out, C4, C5, In3);
  or or_2 (or_2_out, C0, C1, C2);
  or or_3 (or_3_out, C3, C6);
  or or_4 (or_4_out, C1, C4, C6);
  and and_8 (Out3, or_1_out, Selected);
  and and_9 (Out2, or_2_out, Selected);
  and and_10 (Out1, or_3_out, Selected);
  and and_11 (Out0, or_4_out, Selected);

  // Other names for the same wires on the sheet: C7 = In3; S = Selected
endmodule
