// Digital circuit C-part-circuit.dig as structural Verilog
module C_part_circuit (
  input  I1,
  input  W1,
  input  I2,
  input  W2,
  input  I3,
  input  W3,
  input  I4,
  input  W4,
  input  I5,
  input  W5,
  input  I6,
  input  W6,
  input  I7,
  input  W7,
  output R1,
  output R2,
  output R3,
  output R4,
  output R5,
  output R6,
  output R7
);

  xor xor_1 (R1, I1, W1);
  xor xor_2 (R2, I2, W2);
  xor xor_3 (R3, I3, W3);
  xor xor_4 (R4, I4, W4);
  xor xor_5 (R5, I5, W5);
  xor xor_6 (R6, I6, W6);
  xor xor_7 (R7, I7, W7);
endmodule
