// Digital circuit Lab04-01.dig as structural Verilog
module Lab04_01 (
  input  [3:0] In,
  input  [1:0] Selector,
  output [3:0] Output
);

  wire and_1_out, and_2_out, and_3_out, and_4_out, F00, F01, F02, F03, F10, F11, F12, F13, F20, F21, F22,
       F23, F30, F31, F32, F33;

  and and_1 (and_1_out, ~Selector[0], ~Selector[1]);  // And
  and and_2 (and_2_out, Selector[0], ~Selector[1]);  // And
  and and_3 (and_3_out, ~Selector[0], Selector[1]);  // And
  and and_4 (and_4_out, Selector[0], Selector[1]);
  Bin_to_Execess_3 bin_to_execess_3_1 (
    .In0(In[0]), .In1(In[1]), .In2(In[2]), .In3(In[3]), .Selected(and_1_out), .Out3(F00), .Out2(F01),
    .Out1(F02), .Out0(F03));
  Bin_to_Cyclic bin_to_cyclic_1 (
    .In0(In[0]), .In1(In[1]), .In2(In[2]), .In3(In[3]), .Selected(and_2_out), .Out3(F10), .Out2(F11),
    .Out1(F12), .Out0(F13));
  Bin_to_2421 bin_to_2421_1 (
    .In0(In[0]), .In1(In[1]), .In2(In[2]), .In3(In[3]), .Selected(and_3_out), .Out3(F20), .Out2(F21),
    .Out1(F22), .Out0(F23));
  Bin_to_642_3 bin_to_642_3_1 (
    .In0(In[0]), .In1(In[1]), .In2(In[2]), .In3(In[3]), .Selected(and_4_out), .Out3(F30), .Out2(F31),
    .Out1(F32), .Out0(F33));
  or or_1 (Output[0], F00, F10, F20, F30);
  or or_2 (Output[1], F01, F11, F21, F31);
  or or_3 (Output[2], F02, F12, F22, F32);
  or or_4 (Output[3], F03, F13, F23, F33);

  // Other names for the same wires on the sheet: I0 = In[0]; I1 = In[1]; I2 = In[2]; I3 = In[3]; S0 = Selector[0];
  //   S1 = Selector[1]
endmodule
