// Digital circuit Lab04-02.dig as structural Verilog
module Lab04_02 (
  input  [6:0] In,
  output [6:0] Output
);

  wire a_part_circuit_1_c1, a_part_circuit_1_c2, a_part_circuit_1_c3, b_part_circuit_1_w1,
       b_part_circuit_1_w2, b_part_circuit_1_w3, b_part_circuit_1_w4, b_part_circuit_1_w5,
       b_part_circuit_1_w6, b_part_circuit_1_w7;

  A_part_circuit a_part_circuit_1 (
    .I1(In[0]), .I2(In[1]), .I3(In[2]), .I4(In[3]), .I5(In[4]), .I6(In[5]), .I7(In[6]),
    .C1(a_part_circuit_1_c1), .C2(a_part_circuit_1_c2), .C3(a_part_circuit_1_c3));
  B_part_circuit b_part_circuit_1 (
    .C1(a_part_circuit_1_c1), .C2(a_part_circuit_1_c2), .C3(a_part_circuit_1_c3), .W1(b_part_circuit_1_w1),
    .W2(b_part_circuit_1_w2), .W3(b_part_circuit_1_w3), .W4(b_part_circuit_1_w4), .W5(b_part_circuit_1_w5),
    .W6(b_part_circuit_1_w6), .W7(b_part_circuit_1_w7));
  C_part_circuit c_part_circuit_1 (
    .I1(In[0]), .W1(b_part_circuit_1_w1), .I2(In[1]), .W2(b_part_circuit_1_w2), .I3(In[2]),
    .W3(b_part_circuit_1_w3), .I4(In[3]), .W4(b_part_circuit_1_w4), .I5(In[4]), .W5(b_part_circuit_1_w5),
    .I6(In[5]), .W6(b_part_circuit_1_w6), .I7(In[6]), .W7(b_part_circuit_1_w7), .R1(Output[0]),
    .R2(Output[1]), .R3(Output[2]), .R4(Output[3]), .R5(Output[4]), .R6(Output[5]), .R7(Output[6]));
endmodule
